# Fritzing sketch Circuit (saved by Fritzing 0.9.2b)
circuit board: 8.46667cm x 5.64444cm
breadboards: 1

parts:
  Part1 = Arduino Uno (Rev3) - ICSP
  J1 = Peltier Element [part_number=UT15,12,F2,4040]
  J2 = Peltier Element [part_number=TEC1-12706]
  M1 = DC Motor [part_number=Heatsink]
  R1 = Resistor [tolerance=±5% resistance=2.5k package="2010 [SMD]"]
  LED1 = smd LED [color="Green (555nm)" package="0603 [SMD]"]
  Q2 = Basic FET N-Channel [package="D2Pak [SMD]"]
  Q1 = Basic FET N-Channel [package="D2Pak [SMD]"]
  D1 = Rectifier Diode [part_number=1N4001 package="Melf DO-213 AB [SMD]"]
  VCC1 = 4 x AAA Battery Mount [part_number=12V]
  VCC2 = 4 x AAA Battery Mount [part_number=12V]
  VCC3 = 4 x AAA Battery Mount [part_number=12V]

nets:
  N1: Part1.A0, D1.anode
  N2: Part1.A1, D1.cathode
  N3: Part1.GND, M1.pin_1, LED1.cathode, Q2.source, Q1.source, VCC1.-, VCC2.-, VCC3.-
  N4: Part1.D9_PWM, Q2.Gate
  N5: Part1.D10_PWM/SS, R1.Pin_1
  N6: Part1.D3_PWM, Q1.Gate
  N7: Part1.VIN, M1.pin_2, VCC3.+
  N8: J1.pin1, Q1.drain
  N9: J1.pin2, VCC2.+
  N10: J2.pin1, Q2.drain
  N11: J2.pin2, VCC1.+
  N12: R1.Pin_0, LED1.anode
